# Fritzing sketch diagram (saved by Fritzing 0.9.3b)
breadboards: 1

parts:
  Raspberry_Pi_1 = Raspberry Pi 3 [part_number=RPI-3-V1.2]
  S1 = Round Pushbutton
  S2 = Round Pushbutton
  Grove2 = Grove OLED 128x96
  S3 = Round Pushbutton [part_number=Oramge]

nets:
  N1: Raspberry_Pi_1.GPIO2, Grove2.SDA
  N2: Raspberry_Pi_1.GPIO3, Grove2.SCL
  N3: Raspberry_Pi_1.GIPO27, S3.leg1
  N4: Raspberry_Pi_1.GIPO26, S2.leg1
  N5: Raspberry_Pi_1.GIPO16, S1.leg1
  GND: Raspberry_Pi_1.GND, S1.leg0, S2.leg0, Grove2.GND, S3.leg0
  5V: Raspberry_Pi_1.5V, Grove2.VCC
